// Logisim project Logisim-CPU.circ as structural Verilog
module main (
);
endmodule

module J_K_FlipFlop__logisim (
  input  J,
  input  CLK,
  input  K,
  input  S,
  input  Enable,
  input  R,
  output Q
);

  J_K_Flip_Flop j_k_ff_1 (.J(J), .clk(CLK), .K(K), .Q(Q), .preset(S), .en(Enable), .reset(R));  // open: Qn

  // Notes on the sheet:
  //   J-K Flip Flop
endmodule

module Register_16Bit (
  input  S,
  input  Enable,
  input  CLK,
  input  R,
  input  E1,
  input  E2,
  input  E3,
  input  E4,
  input  E5,
  input  E6,
  input  E7,
  input  E8,
  input  E9,
  input  E10,
  input  E11,
  input  E12,
  input  E13,
  input  E14,
  input  E15,
  input  E16,
  output A1,
  output A2,
  output A3,
  output A4,
  output A5,
  output A6,
  output A7,
  output A8,
  output A9,
  output A10,
  output A11,
  output A12,
  output A13,
  output A14,
  output A15,
  output A16
);

  wire not_1_out, not_2_out, not_3_out, not_4_out, not_5_out, not_6_out, not_7_out, not_8_out, not_9_out,
       not_10_out, not_11_out, not_12_out, not_13_out, not_14_out, not_15_out, not_16_out;

  not not_1 (not_1_out, E9);
  not not_2 (not_2_out, E13);
  J_K_FlipFlop__logisim J_K_FlipFlop (.J(E1), .CLK(CLK), .K(not_3_out), .S(S), .Enable(Enable), .R(R), .Q(A1));
  not not_3 (not_3_out, E1);
  not not_4 (not_4_out, E5);
  J_K_FlipFlop__logisim J_K_FlipFlop_2 (.J(E5), .CLK(CLK), .K(not_4_out), .S(S), .Enable(Enable), .R(R), .Q(A5));
  J_K_FlipFlop__logisim J_K_FlipFlop_3 (.J(E9), .CLK(CLK), .K(not_1_out), .S(S), .Enable(Enable), .R(R), .Q(A9));
  J_K_FlipFlop__logisim J_K_FlipFlop_4 (.J(E13), .CLK(CLK), .K(not_2_out), .S(S), .Enable(Enable), .R(R), .Q(A13));
  not not_5 (not_5_out, E2);
  not not_6 (not_6_out, E6);
  not not_7 (not_7_out, E10);
  J_K_FlipFlop__logisim J_K_FlipFlop_5 (.J(E10), .CLK(CLK), .K(not_7_out), .S(S), .Enable(Enable), .R(R), .Q(A10));
  J_K_FlipFlop__logisim J_K_FlipFlop_6 (.J(E14), .CLK(CLK), .K(not_8_out), .S(S), .Enable(Enable), .R(R), .Q(A14));
  not not_8 (not_8_out, E14);
  J_K_FlipFlop__logisim J_K_FlipFlop_7 (.J(E2), .CLK(CLK), .K(not_5_out), .S(S), .Enable(Enable), .R(R), .Q(A2));
  J_K_FlipFlop__logisim J_K_FlipFlop_8 (.J(E6), .CLK(CLK), .K(not_6_out), .S(S), .Enable(Enable), .R(R), .Q(A6));
  not not_9 (not_9_out, E3);
  not not_10 (not_10_out, E7);
  not not_11 (not_11_out, E11);
  not not_12 (not_12_out, E15);
  J_K_FlipFlop__logisim J_K_FlipFlop_9 (.J(E3), .CLK(CLK), .K(not_9_out), .S(S), .Enable(Enable), .R(R), .Q(A3));
  J_K_FlipFlop__logisim J_K_FlipFlop_10 (.J(E7), .CLK(CLK), .K(not_10_out), .S(S), .Enable(Enable), .R(R), .Q(A7));
  J_K_FlipFlop__logisim J_K_FlipFlop_11 (.J(E11), .CLK(CLK), .K(not_11_out), .S(S), .Enable(Enable), .R(R), .Q(A11));
  J_K_FlipFlop__logisim J_K_FlipFlop_12 (.J(E15), .CLK(CLK), .K(not_12_out), .S(S), .Enable(Enable), .R(R), .Q(A15));
  not not_13 (not_13_out, E4);
  not not_14 (not_14_out, E8);
  not not_15 (not_15_out, E12);
  not not_16 (not_16_out, E16);
  J_K_FlipFlop__logisim J_K_FlipFlop_13 (.J(E4), .CLK(CLK), .K(not_13_out), .S(S), .Enable(Enable), .R(R), .Q(A4));
  J_K_FlipFlop__logisim J_K_FlipFlop_14 (.J(E8), .CLK(CLK), .K(not_14_out), .S(S), .Enable(Enable), .R(R), .Q(A8));
  J_K_FlipFlop__logisim J_K_FlipFlop_15 (.J(E12), .CLK(CLK), .K(not_15_out), .S(S), .Enable(Enable), .R(R), .Q(A12));
  J_K_FlipFlop__logisim J_K_FlipFlop_16 (.J(E16), .CLK(CLK), .K(not_16_out), .S(S), .Enable(Enable), .R(R), .Q(A16));
endmodule

module Register_16Bit__logisim (
  input  E1,
  input  E2,
  input  Enable,
  input  E3,
  input  E4,
  input  CLK,
  input  E5,
  input  E6,
  input  R,
  input  E7,
  input  E8,
  input  E9,
  input  E10,
  input  E11,
  input  E12,
  input  E13,
  input  E14,
  input  E15,
  input  E16,
  output A1,
  output A2,
  output A3,
  output A4,
  output A5,
  output A6,
  output A7,
  output A8,
  output A9,
  output A10,
  output A11,
  output A12,
  output A13,
  output A14,
  output A15,
  output A16
);

  Register #(.width(16)) register_1 (
    .D({E16, E15, E14, E13, E12, E11, E10, E9, E8, E7, E6, E5, E4, E3, E2, E1}), .en(Enable),
    .Q({A16, A15, A14, A13, A12, A11, A10, A9, A8, A7, A6, A5, A4, A3, A2, A1}), .clk(CLK), .clr(R));
endmodule

module J_K_FlipFlop (
  input  S,
  input  J,
  input  CLK,
  input  Enable,
  input  K,
  input  R,
  input  in_7,
  input  in_8,
  input  in_9,
  output A,
  output out_11
);

  wire AND_2_out, AND_3_out, AND_out, NAND_2_out, NAND_3_out, NAND_4_out, NAND_5_out, NAND_6_out, NAND_8_out,
       NAND_out, NOT_2_out, NOT_3_out, NOT_4_out, NOT_out;

  and AND (AND_out, CLK, Enable);
  not NOT (NOT_out, AND_out);
  and AND_2 (AND_2_out, in_7, in_8);
  not NOT_2 (NOT_2_out, S);
  nand NAND (NAND_out, NAND_8_out, J, NOT_out);
  nand NAND_2 (NAND_2_out, NOT_out, K, A);
  not NOT_3 (NOT_3_out, NOT_out);
  not NOT_4 (NOT_4_out, R);
  and AND_3 (AND_3_out, AND_2_out, in_9);
  not NOT_5 (out_11, AND_3_out);
  nand NAND_3 (NAND_3_out, NOT_2_out, NAND_out, NAND_4_out);
  nand NAND_4 (NAND_4_out, NAND_3_out, NAND_2_out, NOT_4_out);
  nand NAND_5 (NAND_5_out, NAND_3_out, NOT_3_out);
  nand NAND_6 (NAND_6_out, NOT_3_out, NAND_4_out);
  nand NAND_7 (A, NOT_2_out, NAND_5_out, NAND_8_out);
  nand NAND_8 (NAND_8_out, A, NAND_6_out, NOT_4_out);

  // Notes on the sheet:
  //   NAND (3 Eingänge)
endmodule

module HalbAddierer (
  input  E1,
  input  E2,
  output A,
  output U
);

  wire AND_2_out, AND_out, NOT_2_out, NOT_out;

  not NOT (NOT_out, E1);
  not NOT_2 (NOT_2_out, E2);
  and AND (AND_out, NOT_out, E2);
  and AND_2 (AND_2_out, NOT_2_out, E1);
  or OR (A, AND_out, AND_2_out);
  and AND_3 (U, E2, E1);
endmodule

module Volladdierer (
  input  E1,
  input  E2,
  input  Ue,
  output A,
  output Ua
);

  wire Halbaddierer_2_u, Halbaddierer_a, Halbaddierer_u;

  HalbAddierer Halbaddierer (.E1(E1), .E2(E2), .A(Halbaddierer_a), .U(Halbaddierer_u));
  HalbAddierer Halbaddierer_2 (.E1(Halbaddierer_a), .E2(Ue), .A(A), .U(Halbaddierer_2_u));
  or OR (Ua, Halbaddierer_2_u, Halbaddierer_u);
endmodule

module Addierer16Bit (
  input  Ue,
  input  X1,
  input  Y1,
  input  X2,
  input  Y2,
  input  X3,
  input  Y3,
  input  X4,
  input  Y4,
  input  X5,
  input  Y5,
  input  X6,
  input  Y6,
  input  X7,
  input  Y7,
  input  X8,
  input  Y8,
  input  X9,
  input  Y9,
  input  X10,
  input  Y10,
  input  X11,
  input  Y11,
  input  X12,
  input  Y12,
  input  X13,
  input  Y13,
  input  X14,
  input  Y14,
  input  X15,
  input  Y15,
  input  X16,
  input  Y16,
  output A1,
  output A2,
  output A3,
  output A4,
  output A5,
  output A6,
  output A7,
  output A8,
  output A9,
  output A10,
  output A11,
  output A12,
  output Ua,
  output A13,
  output A14,
  output A15,
  output A16
);

  wire Volladdierer_2_ua, Volladdierer_3_ua, Volladdierer_4_ua, Volladdierer_5_ua, Volladdierer_6_ua,
       Volladdierer_7_ua, Volladdierer_8_ua, Volladdierer_9_ua, Volladdierer_10_ua, Volladdierer_11_ua,
       Volladdierer_12_ua, Volladdierer_13_ua, Volladdierer_14_ua, Volladdierer_15_ua, Volladdierer_ua;

  Volladdierer Volladdierer (.E1(Y1), .E2(X1), .Ue(Ue), .A(A1), .Ua(Volladdierer_ua));
  Volladdierer Volladdierer_2 (.E1(Y5), .E2(X5), .Ue(Volladdierer_13_ua), .A(A5), .Ua(Volladdierer_2_ua));
  Volladdierer Volladdierer_3 (.E1(Y9), .E2(X9), .Ue(Volladdierer_14_ua), .A(A9), .Ua(Volladdierer_3_ua));
  Volladdierer Volladdierer_4 (.E1(Y13), .E2(X13), .Ue(Volladdierer_15_ua), .A(A13), .Ua(Volladdierer_4_ua));
  Volladdierer Volladdierer_5 (.E1(Y2), .E2(X2), .Ue(Volladdierer_ua), .A(A2), .Ua(Volladdierer_5_ua));
  Volladdierer Volladdierer_6 (.E1(Y6), .E2(X6), .Ue(Volladdierer_2_ua), .A(A6), .Ua(Volladdierer_6_ua));
  Volladdierer Volladdierer_7 (.E1(Y10), .E2(X10), .Ue(Volladdierer_3_ua), .A(A10), .Ua(Volladdierer_7_ua));
  Volladdierer Volladdierer_8 (.E1(Y14), .E2(X14), .Ue(Volladdierer_4_ua), .A(A14), .Ua(Volladdierer_8_ua));
  Volladdierer Volladdierer_9 (.E1(Y3), .E2(X3), .Ue(Volladdierer_5_ua), .A(A3), .Ua(Volladdierer_9_ua));
  Volladdierer Volladdierer_10 (.E1(Y7), .E2(X7), .Ue(Volladdierer_6_ua), .A(A7), .Ua(Volladdierer_10_ua));
  Volladdierer Volladdierer_11 (.E1(Y11), .E2(X11), .Ue(Volladdierer_7_ua), .A(A11), .Ua(Volladdierer_11_ua));
  Volladdierer Volladdierer_12 (.E1(Y15), .E2(X15), .Ue(Volladdierer_8_ua), .A(A15), .Ua(Volladdierer_12_ua));
  Volladdierer Volladdierer_13 (.E1(Y4), .E2(X4), .Ue(Volladdierer_9_ua), .A(A4), .Ua(Volladdierer_13_ua));
  Volladdierer Volladdierer_14 (.E1(Y8), .E2(X8), .Ue(Volladdierer_10_ua), .A(A8), .Ua(Volladdierer_14_ua));
  Volladdierer Volladdierer_15 (.E1(Y12), .E2(X12), .Ue(Volladdierer_11_ua), .A(A12), .Ua(Volladdierer_15_ua));
  Volladdierer Volladdierer_16 (.E1(Y16), .E2(X16), .Ue(Volladdierer_12_ua), .A(A16), .Ua(Ua));
endmodule

module Addierer16Bit_logisim (
  input  Ue,
  input  [15:0] X_1_16,
  input  [15:0] Y_1_16,
  output [15:0] A_1_16,
  output Ua
);

  Adder #(.width(16)) adder_1 (.a(X_1_16), .b(Y_1_16), .out(A_1_16), .cin(Ue), .cout(Ua));
endmodule

module ProgramCounter (
  input  [15:0] imidiatly_Reg,
  input  [1:0] PC_select,
  input  PC_load,
  input  Reset,
  input  [15:0] static_Reg,
  output [15:0] PC_out
);

  wire Takt_out;
  wire [15:0] adder_1_out, adder_2_out, multiplexer_1_out;

  Adder #(.width(16)) adder_1 (.a(PC_out), .b(16'h1), .out(adder_1_out));  // open: cin, cout
  Adder #(.width(16)) adder_2 (.a(imidiatly_Reg), .b(PC_out), .out(adder_2_out));  // open: cin, cout
  Multiplexer #(.select(2), .width(16), .enable("false")) multiplexer_1 (
    .in0(adder_1_out), .in1(imidiatly_Reg), .in2(adder_2_out), .in3(static_Reg), .out(multiplexer_1_out),
    .sel(PC_select));
  Register #(.width(16)) register_1 (.D(multiplexer_1_out), .en(PC_load), .Q(PC_out), .clk(Takt_out), .clr(Reset));
  Clock Takt (.out(Takt_out));

  // Notes on the sheet:
  //   Addierer
  //   Addierer
  //   Multiplexer
  //   Register
endmodule
